// Logisim project ALU.circ as structural Verilog: 2 circuits, main circuit Multiplier S
module Multiplier_S (
  input  [31:0] in_1,
  input  [31:0] in_2,
  output [31:0] out_3,
  output [31:0] out_4
);

  wire C_plus, S_OUT;
  wire [31:0] A_M, adder_1_out, adder_2_out, B_M, bit_extender_1_out, Carry, negator_1_out, negator_2_out,
       not_1_out, not_2_out, Prod;

  xor xor_1 (S_OUT, in_2[31], in_1[31]);
  assign not_1_out = ~Prod;  // NOT_Gate not_1, 32 bits wide
  assign not_2_out = ~Carry;  // NOT_Gate not_2, 32 bits wide
  Negator #(.width(32)) negator_1 (.in(in_1), .out(negator_1_out));
  Negator #(.width(32)) negator_2 (.in(in_2), .out(negator_2_out));
  Adder #(.width(32)) adder_1 (.a(not_1_out), .b(32'h1), .out(adder_1_out), .cout(C_plus));  // open: cin
  assign bit_extender_1_out = {{31{1'b0}}, C_plus};  // Bit_Extender bit_extender_1
  Multiplexer #(.width(32), .enable("false")) multiplexer_1 (
    .in0(in_1), .in1(negator_1_out), .out(A_M), .sel(in_1[31]));
  Multiplexer #(.width(32), .enable("false")) multiplexer_2 (
    .in0(in_2), .in1(negator_2_out), .out(B_M), .sel(in_2[31]));
  Adder #(.width(32)) adder_2 (.a(not_2_out), .b(bit_extender_1_out), .out(adder_2_out));  // open: cin, cout
  Multiplexer #(.width(32), .enable("false")) multiplexer_3 (.in0(Prod), .in1(adder_1_out), .out(out_3), .sel(S_OUT));
  Multiplexer #(.width(32), .enable("false")) multiplexer_4 (.in0(Carry), .in1(adder_2_out), .out(out_4), .sel(S_OUT));
  Multiplier #(.width(32)) multiplier_1 (.a(A_M), .b(B_M), .out(Prod), .cout(Carry));  // open: cin

  // Other names for the same wires on the sheet: A[31:0] = in_1; S_A = in_1[31]; B[31:0] = in_2; S_B = in_2[31];
  //   M[31:0] = out_3; M_C[31:0] = out_4

  // Notes on the sheet:
  //   MULTIPLIER
  //   IGNED
  //   S
endmodule

module Divider_S (
  input  [31:0] in_1,
  input  [31:0] in_2,
  output [31:0] out_3,
  output [31:0] out_4
);

  wire C_plus, S_OUT;
  wire [31:0] A_M, adder_1_out, adder_2_out, B_M, bit_extender_1_out, Carry, Div, negator_1_out,
       negator_2_out, not_1_out, not_2_out;

  xor xor_1 (S_OUT, in_2[31], in_1[31]);
  Negator #(.width(32)) negator_1 (.in(in_1), .out(negator_1_out));
  Negator #(.width(32)) negator_2 (.in(in_2), .out(negator_2_out));
  assign not_1_out = ~Div;  // NOT_Gate not_1, 32 bits wide
  Adder #(.width(32)) adder_1 (.a(not_1_out), .b(32'h1), .out(adder_1_out), .cout(C_plus));  // open: cin
  assign not_2_out = ~Carry;  // NOT_Gate not_2, 32 bits wide
  assign bit_extender_1_out = {{31{1'b0}}, C_plus};  // Bit_Extender bit_extender_1
  Multiplexer #(.width(32), .enable("false")) multiplexer_1 (
    .in0(in_1), .in1(negator_1_out), .out(A_M), .sel(in_1[31]));
  Multiplexer #(.width(32), .enable("false")) multiplexer_2 (
    .in0(in_2), .in1(negator_2_out), .out(B_M), .sel(in_2[31]));
  Adder #(.width(32)) adder_2 (.a(not_2_out), .b(bit_extender_1_out), .out(adder_2_out));  // open: cin, cout
  Multiplexer #(.width(32), .enable("false")) multiplexer_3 (.in0(Div), .in1(adder_1_out), .out(out_3), .sel(S_OUT));
  Multiplexer #(.width(32), .enable("false")) multiplexer_4 (.in0(Carry), .in1(adder_2_out), .out(out_4), .sel(S_OUT));
  Divider #(.width(32)) divider_1 (.a(A_M), .b(B_M), .out(Div), .rem(Carry));  // open: upper

  // Other names for the same wires on the sheet: A[31:0] = in_1; S_A = in_1[31]; B[31:0] = in_2; S_B = in_2[31];
  //   D[31:0] = out_3; D_C[31:0] = out_4

  // Notes on the sheet:
  //   DIVIDER
  //   IGNED
  //   S
endmodule
