// Logisim project Control Unit.circ as structural Verilog: 4 circuits, main circuit Control Unit
module Control_Unit (
  input  in_1,
  input  in_2,
  input  [5:0] in_3,
  input  [5:0] in_4,
  input  [3:0] in_5,
  input  [3:0] in_6,
  output Output,
  output [2:0] out_8,
  output out_9,
  output [1:0] out_10,
  output out_11,
  output out_12,
  output out_13,
  output out_14,
  output out_15,
  output out_16,
  output out_17,
  output out_18,
  output out_19,
  output out_20,
  output out_21,
  output out_22,
  output out_23,
  output [2:0] out_24,
  output [3:0] out_25,
  output [2:0] out_26
);

  wire Aritmetic, Aritmetic_End, CS_1, CS_2, CS_3, CS_4, CS_5, CS_6, CS_7, d_ff_1_q, d_ff_2_q, d_ff_8_q,
       d_ff_10_q, d_ff_12_q, d_ff_16_q, d_ff_17_q, d_ff_18_q, d_ff_19_q, d_ff_24_q, d_ff_29_q, Halt, Hi,
       Hi_End, I_Basic, Kbd, L_A_B_2, L_A_B_3, L_A_B_6, L_A_B_7, L_A_B_8, L_Hi_0, L_Hi_1, L_Hi_2, L_Hi_3,
       L_Hi_4, L_Hi_5, L_Hi_6, L_Hi_7, Lo_End, Load_W_End, M_D, MemToR0_2, MemToR2_1, nor_1_out, or_1_out,
       or_2_out, or_4_out, or_5_out, or_6_out, or_7_out, or_10_out, Pop, Pop_End, PP_Sel, Push, Push_End,
       Push_Pop_End, R_Basic, R_W_RF_0, R_W_RF_1, R_W_RF_6, RT__WT_RAM_Sel, Sel_B__ALU__0_0, Sel_B__ALU__2_2,
       Special, Special_End, Store_W, Store_W_End, Wait_For_Ram;
  wire [1:0] Aritmetic_Sel, Special_Op_Sel;
  wire [2:0] Op_Sel;
  wire [3:0] counter_1_q, RT__WT;

  Multiplexer #(.width(4), .enable("false")) multiplexer_1 (.in0(in_6), .in1(in_5), .out(RT__WT), .sel(RT__WT_RAM_Sel));
  D_Flip_Flop d_ff_1 (.clk(in_1), .D(1'b0), .Q(d_ff_1_q), .preset(in_2));  // open: Qn, en, reset
  Demultiplexer #(.select(2), .enable("false")) demultiplexer_1 (
    .out0(Halt), .out1(MemToR2_1), .out2(L_A_B_3), .out3(Kbd), .in(Special), .sel(Special_Op_Sel));
  Counter #(.width(4), .max('hf)) counter_1 (
    .load(out_12), .D(RT__WT), .count(d_ff_2_q), .Q(counter_1_q), .clk(in_1));  // open: carry, clr
  D_Flip_Flop d_ff_2 (.clk(in_1), .D(out_12), .Q(d_ff_2_q), .reset(in_2));  // open: Qn, preset, en
  or or_1 (or_1_out, out_23, d_ff_1_q);
  Demultiplexer #(.select(2), .enable("false")) demultiplexer_2 (
    .out0(R_Basic), .out1(M_D), .out2(I_Basic), .in(Aritmetic), .sel(Aritmetic_Sel));  // open: out3
  D_Flip_Flop d_ff_3 (.clk(in_1), .D(Hi), .Q(Hi_End), .reset(in_2));  // open: Qn, preset, en
  D_Flip_Flop d_ff_4 (.clk(in_1), .D(L_A_B_6), .Q(L_Hi_6), .reset(in_2));  // open: Qn, preset, en
  Demultiplexer #(.enable("false")) demultiplexer_3 (.out0(Push), .out1(Pop), .in(out_22), .sel(PP_Sel));
  D_Flip_Flop d_ff_5 (.clk(in_1), .D(Push), .Q(L_Hi_3), .reset(in_2));  // open: Qn, preset, en
  D_Flip_Flop d_ff_6 (.clk(in_1), .D(Pop), .Q(L_Hi_4), .reset(in_2));  // open: Qn, preset, en
  nor nor_1 (nor_1_out, counter_1_q[0], counter_1_q[1], counter_1_q[2], counter_1_q[3]);
  or or_2 (or_2_out, CS_7, or_1_out);
  D_Flip_Flop d_ff_7 (.clk(in_1), .D(L_A_B_7), .Q(L_Hi_7), .reset(in_2));  // open: Qn, preset, en
  or or_3 (RT__WT_RAM_Sel, CS_1, CS_6);
  and and_1 (Wait_For_Ram, nor_1_out, d_ff_2_q);
  D_Flip_Flop d_ff_8 (.clk(in_1), .D(or_2_out), .Q(d_ff_8_q), .reset(in_2));  // open: Qn, preset, en
  D_Flip_Flop d_ff_9 (.clk(in_1), .D(Halt), .Q(Output), .en(Halt), .reset(in_2));  // open: Qn, preset
  D_Flip_Flop d_ff_10 (.clk(in_1), .D(L_Hi_7), .Q(d_ff_10_q), .reset(in_2));  // open: Qn, preset, en
  D_Flip_Flop d_ff_11 (.clk(in_1), .D(L_Hi_3), .Q(R_W_RF_6), .reset(in_2));  // open: Qn, preset, en
  D_Flip_Flop d_ff_12 (.clk(in_1), .D(L_Hi_4), .Q(d_ff_12_q), .reset(in_2));  // open: Qn, preset, en
  Demultiplexer #(.enable("false")) demultiplexer_4 (.out0(CS_7), .out1(out_19), .in(d_ff_8_q), .sel(Wait_For_Ram));
  D_Flip_Flop d_ff_13 (.clk(in_1), .D(R_Basic), .Q(L_Hi_0), .reset(in_2));  // open: Qn, preset, en
  D_Flip_Flop d_ff_14 (.clk(in_1), .D(M_D), .Q(L_Hi_1), .reset(in_2));  // open: Qn, preset, en
  D_Flip_Flop d_ff_15 (.clk(in_1), .D(I_Basic), .Q(L_Hi_2), .reset(in_2));  // open: Qn, preset, en
  D_Flip_Flop d_ff_16 (.clk(in_1), .D(L_Hi_6), .Q(d_ff_16_q), .reset(in_2));  // open: Qn, preset, en
  or or_4 (or_4_out, CS_4, d_ff_16_q);
  or or_5 (or_5_out, CS_6, d_ff_10_q);
  ALU_Encoder alu_encoder_1 (.Input(in_4), .in_2(in_3), .out_3(out_25));
  Demultiplexer #(.enable("false")) demultiplexer_5 (.out0(CS_4), .out1(CS_5), .in(d_ff_17_q), .sel(Wait_For_Ram));
  D_Flip_Flop d_ff_17 (.clk(in_1), .D(or_4_out), .Q(d_ff_17_q), .reset(in_2));  // open: Qn, preset, en
  Demultiplexer #(.enable("false")) demultiplexer_6 (
    .out0(CS_6), .out1(Store_W_End), .in(d_ff_18_q), .sel(Wait_For_Ram));
  D_Flip_Flop d_ff_18 (.clk(in_1), .D(or_5_out), .Q(d_ff_18_q), .reset(in_2));  // open: Qn, preset, en
  D_Flip_Flop d_ff_19 (.clk(in_1), .D(or_6_out), .Q(d_ff_19_q), .reset(in_2));  // open: Qn, preset, en
  or or_6 (or_6_out, CS_2, d_ff_12_q);
  D_Flip_Flop d_ff_20 (.clk(in_1), .D(L_Hi_0), .Q(R_W_RF_0), .reset(in_2));  // open: Qn, preset, en
  D_Flip_Flop d_ff_21 (.clk(in_1), .D(L_Hi_1), .Q(out_20), .reset(in_2));  // open: Qn, preset, en
  D_Flip_Flop d_ff_22 (.clk(in_1), .D(L_A_B_3), .Q(out_13), .reset(in_2));  // open: Qn, preset, en
  D_Flip_Flop d_ff_23 (.clk(in_1), .D(R_W_RF_6), .Q(out_21), .reset(in_2));  // open: Qn, preset, en
  Demultiplexer #(.enable("false")) demultiplexer_7 (.out0(CS_2), .out1(CS_3), .in(d_ff_19_q), .sel(Wait_For_Ram));
  Branch_Encoder branch_encoder_1 (.in_1(in_4), .in_2(in_3), .out_3(out_24));
  D_Flip_Flop d_ff_24 (.clk(in_1), .D(out_19), .Q(d_ff_24_q), .reset(in_2));  // open: Qn, preset, en
  Demultiplexer #(.select(3), .enable("false")) demultiplexer_8 (
    .out0(Aritmetic), .out1(Hi), .out2(L_A_B_2), .out3(Special), .out4(out_22), .out5(L_A_B_6),
    .out6(Store_W), .out7(L_A_B_8), .in(d_ff_24_q), .sel(Op_Sel));
  D_Flip_Flop d_ff_25 (.clk(in_1), .D(L_Hi_2), .Q(R_W_RF_1), .reset(in_2));  // open: Qn, preset, en
  D_Flip_Flop d_ff_26 (.clk(in_1), .D(L_A_B_2), .Q(Lo_End), .reset(in_2));  // open: Qn, preset, en
  D_Flip_Flop d_ff_27 (.clk(in_1), .D(Kbd), .Q(out_14), .reset(in_2));  // open: Qn, preset, en
  D_Flip_Flop d_ff_28 (.clk(in_1), .D(CS_5), .Q(Load_W_End), .reset(in_2));  // open: Qn, preset, en
  or or_7 (or_7_out, CS_1, out_21);
  CU_Op_Encoder cu_op_encoder_1 (
    .Input(in_4), .in_2(in_3), .out_6(Op_Sel), .out_3(PP_Sel), .out_4(Special_Op_Sel), .out_5(Aritmetic_Sel));
  or or_8 (Aritmetic_End, R_W_RF_0, out_20, R_W_RF_1);
  or or_9 (Special_End, MemToR2_1, out_13, out_14);
  Demultiplexer #(.enable("false")) demultiplexer_9 (.out0(CS_1), .out1(Push_End), .in(d_ff_29_q), .sel(Wait_For_Ram));
  D_Flip_Flop d_ff_29 (.clk(in_1), .D(or_7_out), .Q(d_ff_29_q), .reset(in_2));  // open: Qn, preset, en
  D_Flip_Flop d_ff_30 (.clk(in_1), .D(CS_3), .Q(MemToR0_2), .reset(in_2));  // open: Qn, preset, en
  D_Flip_Flop d_ff_31 (.clk(in_1), .D(MemToR0_2), .Q(L_Hi_5), .reset(in_2));  // open: Qn, preset, en
  or or_10 (or_10_out, Aritmetic_End, Hi_End, Lo_End, Special_End, Push_Pop_End, Load_W_End, Store_W_End, L_A_B_8);
  or or_11 (out_17, CS_1, CS_6, 1'b0);
  or or_12 (out_26[2], L_Hi_3, L_Hi_4, Sel_B__ALU__2_2);
  or or_13 (Push_Pop_End, Push_End, Pop_End);
  D_Flip_Flop End (.clk(in_1), .D(or_10_out), .Q(out_23), .reset(in_2));  // open: Qn, preset, en
  or or_14 (out_11, Aritmetic, Hi, L_A_B_2, L_A_B_3, out_22, out_21, L_A_B_6, L_A_B_7, L_A_B_8);
  or or_15 (out_12, out_19, CS_1, CS_2, CS_3, CS_4, CS_5, CS_6, CS_7, 1'b0);
  or or_16 (out_9, R_W_RF_0, R_W_RF_1, Hi_End, Lo_End, MemToR2_1, Kbd, R_W_RF_6, MemToR0_2, Pop_End, Load_W_End);
  or or_17 (out_16, L_Hi_0, L_Hi_1, L_Hi_2, L_Hi_3, L_Hi_4, L_Hi_5, L_Hi_6, L_Hi_7);
  or or_18 (out_18, CS_1, CS_2, CS_3, CS_4, CS_5, CS_6);
  or or_19 (out_26[0], Sel_B__ALU__0_0, L_Hi_4, L_Hi_6, L_Hi_7);
  D_Flip_Flop d_ff_32 (.clk(in_1), .D(L_Hi_5), .Q(Pop_End), .reset(in_2));  // open: Qn, preset, en
  or or_20 (out_15, CS_3, CS_5);
  or or_21 (out_10[1], R_W_RF_6, Pop_End);
  or or_22 (out_8[0], Hi_End, Kbd, MemToR0_2, Load_W_End);
  or or_23 (out_8[1], Hi_End, Lo_End);
  or or_24 (out_8[2], Kbd, MemToR2_1);
  or or_25 (out_10[0], R_W_RF_0, MemToR2_1, Hi_End, Lo_End, Kbd, MemToR0_2);

  assign out_26[1] = 1'b0;

  // Other names for the same wires on the sheet: ALU_Op[3:0] = out_25; Branch_Code[2:0] = out_24; Clock = in_1;
  //   CS = out_12; DW = out_15; END = Output; Func_Code[5:0] = in_3; I_v_D = out_18; I_v_D_1 = CS_2; DW_0 = CS_3;
  //   I_v_D_2 = CS_3; I_v_D_3 = CS_4; DW_1 = CS_5; I_v_D_4 = CS_5; CS_0 = out_19; Inst_W = out_19; Kbd_EN = out_14;
  //   L_A_B = out_11; L_A_B_0 = Aritmetic; L_A_B_1 = Hi; L_Hi = out_16; Lo = L_A_B_2; Load_W = L_A_B_6;
  //   Mem_W = out_17; Op_Code[5:0] = in_4; End_t = out_23; PC_EN = out_23; R_Time[3:0] = in_6; R_W_RF = out_9;
  //   MemToR0_3 = Load_W_End; R_W_RF_9 = Load_W_End; RDt_0_0 = R_W_RF_0; MemToR0_0 = Hi_End; MemToR1_0 = Hi_End;
  //   R_W_RF_2 = Hi_End; RDt_0_2 = Hi_End; MemToR1_1 = Lo_End; R_W_RF_3 = Lo_End; RDt_0_3 = Lo_End; MemToR0_1 = Kbd;
  //   MemToR2_0 = Kbd; R_W_RF_5 = Kbd; RDt_0_4 = Kbd; R_W_RF_7 = MemToR0_2; RDt_0_5 = MemToR0_2; RDt_1_0 = R_W_RF_6;
  //   R_W_RF_8 = Pop_End; RDt_1_1 = Pop_End; Reset = in_2; R_W_RF_4 = MemToR2_1; RDt_0_1 = MemToR2_1; Rnd = MemToR2_1;
  //   I_v_D_0 = CS_1; Mem_W_0 = CS_1; RT_WT_RAM_Sel_0 = CS_1; I_v_D_5 = CS_6; Mem_W_1 = CS_6; RT_WT_RAM_Sel_1 = CS_6;
  //   L_A_B_4 = out_22; Push_Pop = out_22; S_A__RF = out_22; L_A_B_5 = out_21; S_B_RF = out_21; MemToR0 = out_8[0];
  //   S_Data__RF[2:0] = out_8; MemToR1 = out_8[1]; MemToR2 = out_8[2]; RDt_0 = out_10[0]; S_Rd__RF[1:0] = out_10;
  //   RDt_1 = out_10[1]; Saltos = L_A_B_8; Saltos_End = L_A_B_8; Sel_B__ALU (some bits) = {out_26[2], out_26[0]};
  //   Sel_B__ALU__0 = out_26[0]; Sel_B__ALU__2 = out_26[2]; Sel_B__ALU__0_0_t = L_Hi_2; Sel_B__ALU__0_2 = L_Hi_6;
  //   Sel_B__ALU__0_3 = L_Hi_7; Sel_B__ALU__2_0 = L_Hi_3; Sel_B__ALU__0_1 = L_Hi_4; Sel_B__ALU__2_1 = L_Hi_4;
  //   Sel_B__ALU__2_2_t = L_Hi_5; Store_W_t = L_A_B_7; Tty = L_A_B_3; Tty_EN = out_13; W_H_L = out_20;
  //   W_Time[3:0] = in_5

  // Notes on the sheet:
  //   Input
  //   Wait For Ram
  //   Aritmetic
  //   Hi
  //   Special R
  //   Load W 
  //   Store W 
  //   Push/Pop
  //   General 
  //   Control Unit
  //   ALU-Code
  //   Lo
  //   Branch-Code
  //   CU-Sel
  //   Jump
  //   Output Flags
endmodule

module ALU_Encoder (
  input  [5:0] Input,
  input  [5:0] in_2,
  output [3:0] out_3
);

  wire A_value, add, add_ALU, addi, \and , and_ALU, andi, beq, bgtz, blez, bltz, bne, div, divu, halt, j, jr,
       kbd, lw, mfhi, mflo, mflo_hi, mult, mulu, nop, \nor , \or , or_ALU, ori, Pop, Pop_t, pop_t_t, Push,
       push_pop, Push_t, push_t_t, rnd, slt, slt_ALU, slti, sltiu, sltu, sltu_ALU, sub, sub_ALU, sw, tty,
       \xor , xor_ALU, xori;

  or or_1 (and_ALU, \and , andi);
  or or_2 (slt_ALU, slt, slti);
  or or_3 (xor_ALU, \xor , xori);
  Priority_Encoder #(.select(4)) priority_encoder_1 (
    .in0(mult), .in1(mulu), .in2(div), .in3(divu), .in4(and_ALU), .in5(sub_ALU), .in6(xor_ALU),
    .in7(add_ALU), .in8(or_ALU), .in9(sltu_ALU), .in10(\nor ), .in11(slt_ALU), .in12(mflo_hi),
    .in13(A_value), .out(out_3));  // open: in14, in15, gs, en_out, en_in
  or or_4 (add_ALU, lw, add, Pop, addi, sw);
  or or_5 (or_ALU, \or , ori);
  or or_6 (sltu_ALU, sltu, sltiu);
  or or_7 (mflo_hi, mflo, mfhi);
  or or_8 (sub_ALU, beq, sub, bne, Push);
  or or_9 (A_value, blez, bltz, bgtz);
  and and_1 (add, ~in_2[0], ~in_2[1], ~in_2[2], ~in_2[3], ~in_2[4], in_2[5]);  // AND_Gate
  and and_2 (div, ~in_2[0], in_2[1], ~in_2[2], in_2[3], in_2[4], ~in_2[5]);  // AND_Gate
  and and_3 (\nor , in_2[0], in_2[1], in_2[2], ~in_2[3], ~in_2[4], in_2[5]);  // AND_Gate
  and and_4 (sub, ~in_2[0], in_2[1], ~in_2[2], ~in_2[3], ~in_2[4], in_2[5]);  // AND_Gate
  and and_5 (divu, in_2[0], in_2[1], ~in_2[2], in_2[3], in_2[4], ~in_2[5]);  // AND_Gate
  and and_6 (\xor , ~in_2[0], ~in_2[1], ~in_2[2], in_2[3], ~in_2[4], in_2[5]);  // AND_Gate
  and and_7 (mult, ~in_2[0], ~in_2[1], ~in_2[2], in_2[3], in_2[4], ~in_2[5]);  // AND_Gate
  and and_8 (\and , ~in_2[0], ~in_2[1], in_2[2], ~in_2[3], ~in_2[4], in_2[5]);  // AND_Gate
  and and_9 (slt, ~in_2[0], in_2[1], ~in_2[2], in_2[3], ~in_2[4], in_2[5]);  // AND_Gate
  and and_10 (mulu, in_2[0], ~in_2[1], ~in_2[2], in_2[3], in_2[4], ~in_2[5]);  // AND_Gate
  and and_11 (\or , in_2[0], ~in_2[1], in_2[2], ~in_2[3], ~in_2[4], in_2[5]);  // AND_Gate
  and and_12 (sltu, in_2[0], in_2[1], ~in_2[2], in_2[3], ~in_2[4], in_2[5]);  // AND_Gate
  and and_13 (halt, in_2[0], in_2[1], in_2[2], in_2[3], in_2[4], in_2[5]);
  and and_14 (tty, in_2[0], ~in_2[1], ~in_2[2], ~in_2[3], ~in_2[4], ~in_2[5]);  // AND_Gate
  and and_15 (rnd, ~in_2[0], in_2[1], ~in_2[2], ~in_2[3], ~in_2[4], ~in_2[5]);  // AND_Gate
  and and_16 (kbd, ~in_2[0], ~in_2[1], in_2[2], ~in_2[3], ~in_2[4], ~in_2[5]);  // AND_Gate
  and and_17 (mflo, ~in_2[0], in_2[1], ~in_2[2], ~in_2[3], in_2[4], ~in_2[5]);  // AND_Gate
  and and_18 (mfhi, ~in_2[0], ~in_2[1], ~in_2[2], ~in_2[3], in_2[4], ~in_2[5]);  // AND_Gate
  and and_19 (jr, ~in_2[0], ~in_2[1], ~in_2[2], in_2[3], ~in_2[4], ~in_2[5]);  // AND_Gate
  and and_20 (nop, ~in_2[0], ~in_2[1], ~in_2[2], ~in_2[3], ~in_2[4], ~in_2[5]);  // AND_Gate
  and and_21 (addi, ~Input[0], ~Input[1], ~Input[2], Input[3], ~Input[4], ~Input[5]);  // AND_Gate
  and and_22 (andi, ~Input[0], ~Input[1], Input[2], Input[3], ~Input[4], ~Input[5]);  // AND_Gate
  and and_23 (slti, ~Input[0], Input[1], ~Input[2], Input[3], ~Input[4], ~Input[5]);  // AND_Gate
  and and_24 (sltiu, Input[0], Input[1], ~Input[2], Input[3], ~Input[4], ~Input[5]);  // AND_Gate
  and and_25 (ori, Input[0], ~Input[1], Input[2], Input[3], ~Input[4], ~Input[5]);  // AND_Gate
  and and_26 (xori, ~Input[0], Input[1], Input[2], Input[3], ~Input[4], ~Input[5]);  // AND_Gate
  and and_27 (push_pop, ~Input[0], ~Input[1], ~Input[2], Input[3], Input[4], Input[5]);  // AND_Gate
  and and_28 (push_t_t, in_2[0], ~in_2[1], ~in_2[2], ~in_2[3], ~in_2[4], ~in_2[5]);  // AND_Gate
  and and_29 (pop_t_t, ~in_2[0], ~in_2[1], ~in_2[2], ~in_2[3], ~in_2[4], ~in_2[5]);  // AND_Gate
  and and_30 (Pop_t, pop_t_t, push_pop);
  and and_31 (Push_t, push_pop, push_t_t);
  and and_32 (j, ~Input[0], Input[1], ~Input[2], ~Input[3], ~Input[4], ~Input[5]);  // AND_Gate
  and and_33 (beq, ~Input[0], ~Input[1], Input[2], ~Input[3], ~Input[4], ~Input[5]);  // AND_Gate
  and and_34 (bne, Input[0], ~Input[1], Input[2], ~Input[3], ~Input[4], ~Input[5]);  // AND_Gate
  and and_35 (blez, ~Input[0], Input[1], Input[2], ~Input[3], ~Input[4], ~Input[5]);  // AND_Gate
  and and_36 (bgtz, Input[0], Input[1], Input[2], ~Input[3], ~Input[4], ~Input[5]);  // AND_Gate
  and and_37 (bltz, Input[0], ~Input[1], ~Input[2], ~Input[3], ~Input[4], ~Input[5]);  // AND_Gate
  and and_38 (lw, Input[0], Input[1], ~Input[2], ~Input[3], ~Input[4], Input[5]);  // AND_Gate
  and and_39 (sw, Input[0], Input[1], ~Input[2], Input[3], ~Input[4], Input[5]);  // AND_Gate

  // Other names for the same wires on the sheet: ALU_OP_Code[3:0] = out_3; Func_code[5:0] = in_2;
  //   Op_Code[5:0] = Input

  // Notes on the sheet:
  //   Encoding
  //   Output
  //   ALU Encoder
  //   R-Type ALU
  //   R-Type
  //   R-Type Special
  //   R-Type M
  //   R-Type Other
  //   I-Type
  //   I-Type ALU
  //   R-Type PP
  //   J-Type
  //   I-Type Branch
  //   I-Type L/S
endmodule

module CU_Op_Encoder (
  input  [5:0] Input,
  input  [5:0] in_2,
  output out_3,
  output [1:0] out_4,
  output [1:0] out_5,
  output [2:0] out_6
);

  wire addi, and_6_out, and_9_out, and_16_out, and_18_out, andi, beq, bgtz, blez, bltz, bne, div, divu, halt,
       I_Type_ALU, j, jr, Jumps, kbd, lw, M_D, mfhi, mflo, mult, mulu, N_M_D, nop, or_6_out, ori, push_pop,
       R_Type_Basic, rnd, S_Math, S_Special, slti, sltiu, special, sw, tty, xori;
  wire [1:0] ALU, priority_encoder_1_out;

  Priority_Encoder #(.select(2)) priority_encoder_1 (
    .in0(halt), .in1(rnd), .in2(tty), .in3(kbd), .out(priority_encoder_1_out), .en_out(S_Special));  // open: gs, en_in
  Priority_Encoder #(.select(2)) priority_encoder_2 (
    .in0(N_M_D), .in1(M_D), .in2(I_Type_ALU), .out(ALU), .en_out(S_Math));  // open: in3, gs, en_in
  or or_1 (out_6[0], mfhi, special, lw, Jumps);
  or or_2 (out_6[1], mflo, special, sw, Jumps);
  or or_3 (out_6[2], lw, sw, push_pop, Jumps);
  Multiplexer #(.width(2), .enable("false")) multiplexer_1 (
    .in0(priority_encoder_1_out), .in1(2'b00), .out(out_4), .sel(S_Special));
  Multiplexer #(.width(2), .enable("false")) multiplexer_2 (.in0(ALU), .in1(2'b00), .out(out_5), .sel(S_Math));
  and and_1 (R_Type_Basic, ~Input[0], ~Input[1], ~Input[2], ~Input[3], ~Input[4], ~Input[5]);  // AND_Gate
  and and_2 (divu, in_2[0], in_2[1], ~in_2[2], in_2[3], in_2[4], ~in_2[5]);  // AND_Gate
  and and_3 (div, ~in_2[0], in_2[1], ~in_2[2], in_2[3], in_2[4], ~in_2[5]);  // AND_Gate
  and and_4 (mult, ~in_2[0], ~in_2[1], ~in_2[2], in_2[3], in_2[4], ~in_2[5]);  // AND_Gate
  and and_5 (mulu, in_2[0], ~in_2[1], ~in_2[2], in_2[3], in_2[4], ~in_2[5]);  // AND_Gate
  and and_6 (and_6_out, ~in_2[0], ~in_2[1], ~in_2[2], in_2[3], ~in_2[4], ~in_2[5]);  // AND_Gate
  and and_7 (jr, and_6_out, R_Type_Basic);
  and and_8 (nop, R_Type_Basic, and_9_out);
  and and_9 (and_9_out, ~in_2[0], ~in_2[1], ~in_2[2], ~in_2[3], ~in_2[4], ~in_2[5]);  // AND_Gate
  and and_10 (special, Input[0], Input[1], Input[2], Input[3], Input[4], Input[5]);
  and and_11 (halt, in_2[0], in_2[1], in_2[2], in_2[3], in_2[4], in_2[5]);
  and and_12 (rnd, ~in_2[0], in_2[1], ~in_2[2], ~in_2[3], ~in_2[4], ~in_2[5]);  // AND_Gate
  and and_13 (tty, in_2[0], ~in_2[1], ~in_2[2], ~in_2[3], ~in_2[4], ~in_2[5]);  // AND_Gate
  and and_14 (kbd, ~in_2[0], ~in_2[1], in_2[2], ~in_2[3], ~in_2[4], ~in_2[5]);  // AND_Gate
  and and_15 (mfhi, R_Type_Basic, and_16_out);
  and and_16 (and_16_out, ~in_2[0], ~in_2[1], ~in_2[2], ~in_2[3], in_2[4], ~in_2[5]);  // AND_Gate
  and and_17 (mflo, R_Type_Basic, and_18_out);
  and and_18 (and_18_out, ~in_2[0], in_2[1], ~in_2[2], ~in_2[3], in_2[4], ~in_2[5]);  // AND_Gate
  and and_19 (beq, ~Input[0], ~Input[1], Input[2], ~Input[3], ~Input[4], ~Input[5]);  // AND_Gate
  and and_20 (bne, Input[0], ~Input[1], Input[2], ~Input[3], ~Input[4], ~Input[5]);  // AND_Gate
  and and_21 (blez, ~Input[0], Input[1], Input[2], ~Input[3], ~Input[4], ~Input[5]);  // AND_Gate
  and and_22 (bgtz, Input[0], Input[1], Input[2], ~Input[3], ~Input[4], ~Input[5]);  // AND_Gate
  and and_23 (bltz, Input[0], ~Input[1], ~Input[2], ~Input[3], ~Input[4], ~Input[5]);  // AND_Gate
  and and_24 (push_pop, ~Input[0], ~Input[1], ~Input[2], Input[3], Input[4], Input[5]);  // AND_Gate
  and and_25 (andi, ~Input[0], ~Input[1], Input[2], Input[3], ~Input[4], ~Input[5]);  // AND_Gate
  and and_26 (slti, ~Input[0], Input[1], ~Input[2], Input[3], ~Input[4], ~Input[5]);  // AND_Gate
  and and_27 (sltiu, Input[0], Input[1], ~Input[2], Input[3], ~Input[4], ~Input[5]);  // AND_Gate
  and and_28 (ori, Input[0], ~Input[1], Input[2], Input[3], ~Input[4], ~Input[5]);  // AND_Gate
  and and_29 (xori, ~Input[0], Input[1], Input[2], Input[3], ~Input[4], ~Input[5]);  // AND_Gate
  and and_30 (addi, ~Input[0], ~Input[1], ~Input[2], Input[3], ~Input[4], ~Input[5]);  // AND_Gate
  and and_31 (out_3, ~in_2[0], ~in_2[1], ~in_2[2], ~in_2[3], ~in_2[4], ~in_2[5]);  // AND_Gate
  and and_32 (j, ~Input[0], Input[1], ~Input[2], ~Input[3], ~Input[4], ~Input[5]);  // AND_Gate
  and and_33 (lw, Input[0], Input[1], ~Input[2], ~Input[3], ~Input[4], Input[5]);  // AND_Gate
  and and_34 (sw, Input[0], Input[1], ~Input[2], Input[3], ~Input[4], Input[5]);  // AND_Gate
  or or_4 (Jumps, beq, bne, blez, bgtz, bltz, nop, j, jr);
  or or_5 (I_Type_ALU, sltiu, ori, xori, addi, andi, slti);
  or or_6 (or_6_out, mult, divu, mulu, div);
  and and_35 (M_D, or_6_out, R_Type_Basic);
  and and_36 (N_M_D, ~M_D, R_Type_Basic);  // AND_Gate

  // Other names for the same wires on the sheet: Func_code[5:0] = in_2; Math_OP[1:0] = out_5; Op_Code[5:0] = Input;
  //   Op_CU[2:0] = out_6; Pop = out_3; Special_Op[1:0] = out_4

  // Notes on the sheet:
  //   Encoding
  //   Output
  //   Control Unit Encoder
  //   R-Type ALU
  //   R-Type Other
  //   R-Type
  //   R-Type Special
  //   Decoding
  //   I-Type Branch
  //   I-Type
  //   I-Type ALU
  //   R-Type Push/Pop
  //   J-Type
  //   I-Type L/S
  //   General
endmodule

module Branch_Encoder (
  input  [5:0] in_1,
  input  [5:0] in_2,
  output [2:0] out_3
);

  wire and_2_out, and_4_out, beq, bgtz, blez, bltz, bne, j, jr, nop, R_Type, Sel;
  wire [2:0] Branch_Control;

  and and_1 (R_Type, ~in_1[0], ~in_1[1], ~in_1[2], ~in_1[3], ~in_1[4], ~in_1[5]);  // AND_Gate
  and and_2 (and_2_out, ~in_2[0], ~in_2[1], ~in_2[2], ~in_2[3], ~in_2[4], ~in_2[5]);  // AND_Gate
  and and_3 (nop, and_2_out, R_Type);
  and and_4 (and_4_out, ~in_2[0], ~in_2[1], ~in_2[2], in_2[3], ~in_2[4], ~in_2[5]);  // AND_Gate
  and and_5 (jr, and_4_out, R_Type);
  and and_6 (j, ~in_1[0], in_1[1], ~in_1[2], ~in_1[3], ~in_1[4], ~in_1[5]);  // AND_Gate
  and and_7 (beq, ~in_1[0], ~in_1[1], in_1[2], ~in_1[3], ~in_1[4], ~in_1[5]);  // AND_Gate
  and and_8 (bne, in_1[0], ~in_1[1], in_1[2], ~in_1[3], ~in_1[4], ~in_1[5]);  // AND_Gate
  and and_9 (bgtz, in_1[0], in_1[1], in_1[2], ~in_1[3], ~in_1[4], ~in_1[5]);  // AND_Gate
  and and_10 (bltz, in_1[0], ~in_1[1], ~in_1[2], ~in_1[3], ~in_1[4], ~in_1[5]);  // AND_Gate
  and and_11 (blez, ~in_1[0], in_1[1], in_1[2], ~in_1[3], ~in_1[4], ~in_1[5]);  // AND_Gate
  Priority_Encoder priority_encoder_1 (
    .in0(nop), .in1(beq), .in2(bne), .in3(blez), .in4(bgtz), .in5(bltz), .in6(j), .in7(jr),
    .out(Branch_Control), .en_out(Sel));  // open: en_in, gs
  Multiplexer #(.width(3), .enable("false")) multiplexer_1 (.in0(Branch_Control), .in1(3'b000), .out(out_3), .sel(Sel));

  // Other names for the same wires on the sheet: Branch_Code[2:0] = out_3; Func_code[5:0] = in_2; Op_Code[5:0] = in_1

  // Notes on the sheet:
  //   Input
  //   R-Type
  //   Output
  //   Branch Encoder
  //   Decoding
  //   J-Type
  //   I-Type
  //   Encoding
endmodule
