// Logisim project s-mips.circ as structural Verilog: 11 circuits, main circuit S-MIPS Board
module S_MIPS_Board (
  input  DESHABILITAR_DISPATCHER,
  output halt
);

  wire button_1_out, CLK, CS, d_ff_1_q, LCLR, LoadRAM, LoadRAMOn, LW, R_R_W, R_W, ram_dispatcher_1_finished,
       RCS, Reset_out, RST, TTY_EN;
  wire [2:0] KDB;
  wire [3:0] LMask, Mask, ram_1_read_time, ram_1_write_time, RMask;
  wire [6:0] KDB_DATA, TTY_DATA;
  wire [15:0] Addr, LAddr, RAddr;
  wire [31:0] I0, I1, I2, I3, LData, ram_1_data_out_0, ram_1_data_out_1, ram_1_data_out_2, ram_1_data_out_3,
       RI0, RI1, RI2, RI3;

  TTY #(.rows(25), .cols(80)) tty_1 (.data(TTY_DATA), .clk(CLK), .we(TTY_EN), .clr(RST));
  not not_1 (LoadRAMOn, ram_dispatcher_1_finished);
  RAM_Dispatcher ram_dispatcher_1 (
    .WriteTime(ram_1_write_time), .Clock(CLK), .Data(LData), .Address(LAddr), .Mask(LMask),
    .Finished(ram_dispatcher_1_finished), .Write(LW), .CLR(LCLR));
  Keyboard #(.buflen(64)) keyboard_1 (.clk(CLK), .re(KDB[0]), .avail(KDB[2]), .data(KDB_DATA));  // open: clr
  RAM ram_1 (
    .Address(RAddr), .Data_Out_0(ram_1_data_out_0), .Data_Out_1(ram_1_data_out_1),
    .Data_Out_2(ram_1_data_out_2), .Data_Out_3(ram_1_data_out_3), .Data_In_0(RI0), .Data_In_1(RI1),
    .Data_In_2(RI2), .Data_In_3(RI3), .Mask(RMask), .nRead_Write(R_R_W), .Chip_Select(RCS),
    .Read_Time(ram_1_read_time), .Reset(button_1_out), .Write_Time(ram_1_write_time));
  Button button_1 (.out(button_1_out));
  D_Flip_Flop d_ff_1 (.clk(CLK), .D(1'b1), .Q(d_ff_1_q), .reset(Reset_out));  // open: Qn, preset, en
  Button Reset (.out(Reset_out));
  S_MIPS s_mips_1 (
    .Kbd_Enable(KDB[0]), .Address(Addr), .Kbd_Clear(KDB[1]), .Kbd_Available(KDB[2]), .RAM_In_0(I0),
    .Kbd_ASCII_Data(KDB_DATA), .RAM_In_1(I1), .TTY_Enable(TTY_EN), .RAM_In_2(I2), .RAM_In_3(I3),
    .TTY_ASCII_Data(TTY_DATA), .Reset(RST), .RAM_Out_0(ram_1_data_out_0), .Clock(CLK),
    .RAM_Out_1(ram_1_data_out_1), .Stop(halt), .RAM_Out_2(ram_1_data_out_2), .RAM_Out_3(ram_1_data_out_3),
    .Mask(Mask), .Read_Time(ram_1_read_time), .Write_Time(ram_1_write_time), .nRead_Write(R_W),
    .Chip_Select(CS));
  D_Flip_Flop d_ff_2 (.clk(CLK), .D(d_ff_1_q), .Qn(LCLR), .reset(Reset_out));  // open: Q, preset, en
  or or_1 (RST, LCLR, LoadRAM);
  Clock clock_1 (.out(CLK));
  Multiplexer #(.width(32), .enable("false")) multiplexer_1 (.in0(I0), .in1(LData), .out(RI0), .sel(LoadRAM));
  Multiplexer #(.width(32), .enable("false")) multiplexer_2 (.in0(I1), .in1(LData), .out(RI1), .sel(LoadRAM));
  Multiplexer #(.width(32), .enable("false")) multiplexer_3 (.in0(I2), .in1(LData), .out(RI2), .sel(LoadRAM));
  Multiplexer #(.width(32), .enable("false")) multiplexer_4 (.in0(I3), .in1(LData), .out(RI3), .sel(LoadRAM));
  and and_1 (LoadRAM, ~DESHABILITAR_DISPATCHER, LoadRAMOn);  // AND_Gate
  Multiplexer #(.width(16), .enable("false")) multiplexer_5 (.in0(Addr), .in1(LAddr), .out(RAddr), .sel(LoadRAM));
  Multiplexer #(.width(4), .enable("false")) multiplexer_6 (.in0(Mask), .in1(LMask), .out(RMask), .sel(LoadRAM));
  Multiplexer #(.enable("false")) multiplexer_7 (.in0(CS), .in1(LW), .out(RCS), .sel(LoadRAM));
  Multiplexer #(.enable("false")) multiplexer_8 (.in0(R_W), .in1(LW), .out(R_R_W), .sel(LoadRAM));

  // Notes on the sheet:
  //   NO MODIFICAR
  //   Keyboard
endmodule

module RAM (
  input  [15:0] Address,
  input  [31:0] Data_In_0,
  input  [31:0] Data_In_1,
  input  [31:0] Data_In_2,
  input  [31:0] Data_In_3,
  input  [3:0] Mask,
  input  nRead_Write,
  input  Chip_Select,
  input  Reset,
  output [31:0] Data_Out_0,
  output [31:0] Data_Out_1,
  output [31:0] Data_Out_2,
  output [31:0] Data_Out_3,
  output [3:0] Read_Time,
  output [3:0] Write_Time
);

  wire and_2_out, and_3_out, and_4_out, and_5_out, and_6_out, and_7_out, and_8_out, and_9_out, Changed, CLK,
       comparator_2_eq, comparator_3_eq, comparator_4_eq, comparator_5_eq, comparator_6_eq, Count,
       demultiplexer_3_out0, Idle, Idle_q, Load, Load0, Load1, nand_1_out, or_1_out, or_2_out, or_3_out,
       or_4_out, or_5_out, or_6_out, or_7_out, or_8_out, or_9_out, or_10_out, Proc_q, Update_Mem, Zero_Time;
  wire [3:0] counter_1_q, multiplexer_1_out, subtractor_1_out;
  wire [31:0] register_1_q, register_2_q, register_3_q, register_4_q, register_5_q;

  // Probe on 4'b0011
  // Probe on 4'b0011
  Multiplexer #(.width(4), .enable("false")) multiplexer_1 (
    .in0(4'b0011), .in1(4'b0011), .out(multiplexer_1_out), .sel(nRead_Write));
  or or_1 (or_1_out, Idle, Update_Mem);
  or or_2 (or_2_out, ~Chip_Select, Reset);  // OR_Gate
  Subtractor #(.width(4)) subtractor_1 (.a(multiplexer_1_out), .b(4'b0010), .out(subtractor_1_out));  // open: bin, bout
  Demultiplexer #(.enable("false")) demultiplexer_1 (.out0(Idle), .out1(Load0), .in(Idle_q), .sel(Changed));
  D_Flip_Flop u_Idle (.clk(CLK), .D(or_1_out), .Q(Idle_q), .preset(or_2_out));  // open: Qn, en, reset
  // Probe on counter_1_q
  Counter #(.width(4), .max('hf)) counter_1 (
    .load(Load), .D(subtractor_1_out), .count(Count), .Q(counter_1_q), .clk(CLK), .clr(or_3_out));  // open: carry
  or or_3 (or_3_out, ~Chip_Select, Reset);  // OR_Gate
  Comparator #(.width(4), .mode("unsigned")) comparator_1 (
    .a(4'b0000), .b(counter_1_q), .eq(Zero_Time));  // open: gt, lt
  or or_4 (or_4_out, Count, Load0, Load1);
  Register #(.width(32)) register_1 (.D(Data_In_0), .en(Chip_Select), .Q(register_1_q), .clk(CLK), .clr(or_5_out));
  or or_5 (or_5_out, ~Chip_Select, Reset);  // OR_Gate
  Register #(.width(32)) register_2 (.D(Data_In_1), .en(Chip_Select), .Q(register_2_q), .clk(CLK), .clr(or_6_out));
  or or_6 (or_6_out, ~Chip_Select, Reset);  // OR_Gate
  Register #(.width(32)) register_3 (.D(Data_In_2), .en(Chip_Select), .Q(register_3_q), .clk(CLK), .clr(or_7_out));
  or or_7 (or_7_out, ~Chip_Select, Reset);  // OR_Gate
  Register #(.width(32)) register_4 (.D(Data_In_3), .en(Chip_Select), .Q(register_4_q), .clk(CLK), .clr(or_8_out));
  or or_8 (or_8_out, ~Chip_Select, Reset);  // OR_Gate
  Register #(.width(32)) register_5 (
    .D({{11{1'b1}}, nRead_Write, Mask, Address}), .en(Chip_Select), .Q(register_5_q), .clk(CLK),
    .clr(or_9_out));
  or or_9 (or_9_out, ~Chip_Select, Reset);  // OR_Gate
  D_Flip_Flop Proc (.clk(CLK), .D(or_4_out), .Q(Proc_q), .reset(or_10_out));  // open: Qn, preset, en
  or or_10 (or_10_out, ~Chip_Select, Reset);  // OR_Gate
  Demultiplexer #(.enable("false")) demultiplexer_2 (
    .out0(Count), .out1(Update_Mem), .in(demultiplexer_3_out0), .sel(Zero_Time));
  Demultiplexer #(.enable("false")) demultiplexer_3 (
    .out0(demultiplexer_3_out0), .out1(Load1), .in(Proc_q), .sel(Changed));
  Clock clock_1 (.out(CLK));
  Comparator #(.width(32)) comparator_2 (.a(register_1_q), .b(Data_In_0), .eq(comparator_2_eq));  // open: gt, lt
  Comparator #(.width(32)) comparator_3 (.a(register_2_q), .b(Data_In_1), .eq(comparator_3_eq));  // open: gt, lt
  Comparator #(.width(32)) comparator_4 (.a(register_3_q), .b(Data_In_2), .eq(comparator_4_eq));  // open: gt, lt
  Comparator #(.width(32)) comparator_5 (.a(register_4_q), .b(Data_In_3), .eq(comparator_5_eq));  // open: gt, lt
  Comparator #(.width(32)) comparator_6 (
    .a(register_5_q), .b({{11{1'b1}}, nRead_Write, Mask, Address}), .eq(comparator_6_eq));  // open: gt, lt
  nand nand_1 (nand_1_out, comparator_6_eq, comparator_2_eq, comparator_3_eq, comparator_4_eq, comparator_5_eq);
  and and_1 (Changed, nand_1_out, Chip_Select);
  or or_11 (Load, Count, Load1, Load0);
  and and_2 (and_2_out, Mask[0], Update_Mem, nRead_Write);
  and and_3 (and_3_out, Mask[1], Update_Mem, nRead_Write);
  and and_4 (and_4_out, Mask[2], Update_Mem, nRead_Write);
  and and_5 (and_5_out, Mask[3], Update_Mem, nRead_Write);
  RAM_part #(.addrWidth(16), .dataWidth(32), .bus("separate")) ram_1 (
    .addr(Address), .din(Data_In_0), .data(Data_Out_0), .str(and_2_out), .sel(Chip_Select), .clk(CLK),
    .ld(and_6_out), .clr(Reset));
  and and_6 (and_6_out, ~nRead_Write, Idle);  // AND_Gate
  RAM_part #(.addrWidth(16), .dataWidth(32), .bus("separate")) ram_2 (
    .addr(Address), .din(Data_In_1), .data(Data_Out_1), .str(and_3_out), .sel(Chip_Select), .clk(CLK),
    .ld(and_7_out), .clr(Reset));
  and and_7 (and_7_out, ~nRead_Write, Idle);  // AND_Gate
  RAM_part #(.addrWidth(16), .dataWidth(32), .bus("separate")) ram_3 (
    .addr(Address), .din(Data_In_2), .data(Data_Out_2), .str(and_4_out), .sel(Chip_Select), .clk(CLK),
    .ld(and_8_out), .clr(Reset));
  and and_8 (and_8_out, ~nRead_Write, Idle);  // AND_Gate
  RAM_part #(.addrWidth(16), .dataWidth(32), .bus("separate")) ram_4 (
    .addr(Address), .din(Data_In_3), .data(Data_Out_3), .str(and_5_out), .sel(Chip_Select), .clk(CLK),
    .ld(and_9_out), .clr(Reset));
  and and_9 (and_9_out, ~nRead_Write, Idle);  // AND_Gate

  assign Read_Time = 4'b0011;
  assign Write_Time = 4'b0011;

  // Other names for the same wires on the sheet: M0 = Mask[0]; M1 = Mask[1]; M2 = Mask[2]; M3 = Mask[3];
  //   RW = nRead_Write; CLR = Reset; CS = Chip_Select; Load2 = Count

  // Notes on the sheet:
  //   NO MODIFICAR
  //   excepto quizás los valores RT y WT
  //   BANK0
  //   BANK1
  //   BANK2
  //   BANK3
endmodule

module S_MIPS (
  input  Kbd_Available,
  input  [6:0] Kbd_ASCII_Data,
  input  [31:0] RAM_Out_0,
  input  [31:0] RAM_Out_1,
  input  Reset,
  input  [31:0] RAM_Out_2,
  input  Clock,
  input  [31:0] RAM_Out_3,
  input  [3:0] Read_Time,
  input  [3:0] Write_Time,
  output Kbd_Enable,
  output [15:0] Address,
  output Kbd_Clear,
  output TTY_Enable,
  output [6:0] TTY_ASCII_Data,
  output Stop,
  output [31:0] RAM_In_0,
  output [31:0] RAM_In_1,
  output [31:0] RAM_In_2,
  output [31:0] RAM_In_3,
  output [3:0] Mask,
  output nRead_Write,
  output Chip_Select
);

  wire DW, I_v_D, Inst_W, L_A_B, L_Hi, PC_EN, RW_RF, S_A_RF, S_B_RF, W_H_L;
  wire [1:0] S_DW_RF;
  wire [2:0] B_C, S_B_ALU, S_DATA_RF;
  wire [3:0] ALU_Op;
  wire [5:0] Func_Code, Op_Code;

  Data_Path data_path_1 (
    .Input(Clock), .in_2(Reset), .in_3(RAM_Out_0), .in_4(RAM_Out_1), .in_5(RAM_Out_2), .in_6(RAM_Out_3),
    .in_7(Kbd_ASCII_Data), .in_8(S_DATA_RF), .in_9(ALU_Op), .in_10(B_C), .in_11(S_B_ALU), .in_12(S_DW_RF),
    .in_13(S_A_RF), .in_14(S_B_RF), .in_15(RW_RF), .in_16(W_H_L), .in_17(PC_EN), .in_18(DW), .in_19(Inst_W),
    .in_20(L_Hi), .in_21(L_A_B), .in_22(Kbd_Available), .in_23(I_v_D), .out_24(RAM_In_0), .out_25(Address),
    .out_26(Mask), .out_27(TTY_ASCII_Data), .out_28(Op_Code), .out_29(Func_Code));
  Control_Unit control_unit_1 (
    .in_1(Clock), .in_2(Reset), .in_3(Func_Code), .in_4(Op_Code), .in_5(Write_Time), .in_6(Read_Time),
    .out_17(nRead_Write), .out_25(ALU_Op), .out_16(L_Hi), .out_24(B_C), .out_15(DW), .out_14(Kbd_Enable),
    .out_13(TTY_Enable), .Output(Stop), .out_12(Chip_Select), .out_11(L_A_B), .out_9(RW_RF), .out_22(S_A_RF),
    .out_21(S_B_RF), .out_20(W_H_L), .out_19(Inst_W), .out_18(I_v_D), .out_10(S_DW_RF), .out_8(S_DATA_RF),
    .out_26(S_B_ALU), .out_23(PC_EN));

  assign Kbd_Clear = Reset;
  assign RAM_In_1 = RAM_In_0;
  assign RAM_In_2 = RAM_In_0;
  assign RAM_In_3 = RAM_In_0;

  // Other names for the same wires on the sheet: CLK = Clock; CLR = Reset; CS = Chip_Select;
  //   KBD_AVAIL = Kbd_Available; KBD_DATA[6:0] = Kbd_ASCII_Data; RAM_A[15:0] = Address; Data_RAM[31:0] = RAM_In_0;
  //   RAM_INPUT_0[31:0] = RAM_In_0; RAM_INPUT_1[31:0] = RAM_In_0; RAM_INPUT_2[31:0] = RAM_In_0;
  //   RAM_INPUT_3[31:0] = RAM_In_0; RAM_MASK[3:0] = Mask; RAM_OUTPUT_0[31:0] = RAM_Out_0;
  //   RAM_OUTPUT_1[31:0] = RAM_Out_1; RAM_OUTPUT_2[31:0] = RAM_Out_2; RAM_OUTPUT_3[31:0] = RAM_Out_3;
  //   RW = nRead_Write; TTY_DATA[6:0] = TTY_ASCII_Data

  // Notes on the sheet:
  //   RAM ADDRESS
  //   DATA FROM RAM
  //   DATA TO RAM
  //   DATA WRITE MASK
  //   RAM TIMING
  //   RAM CONTROL
  //   KEYBOARD
  //   TTY
  //   SEQUENCING
endmodule

module RAM_Dispatcher (
  input  [3:0] WriteTime,
  input  Clock,
  input  CLR,
  output [31:0] Data,
  output [15:0] Address,
  output [3:0] Mask,
  output Finished,
  output Write
);

  wire demultiplexer_2_out1, demultiplexer_3_out1, End, IDLE_q, IncAddr, Load, or_1_out, or_2_out, While_q,
       WriteEnd;
  wire [3:0] counter_1_q;
  wire [31:0] CurrentAddress_q;

  Counter #(.width(32), .max('hffffffff)) CurrentAddress (
    .count(IncAddr), .Q({CurrentAddress_q[31:18], Address, CurrentAddress_q[1:0]}), .clk(Clock), .clr(CLR));  // open: load, D, carry
  or or_1 (or_1_out, IncAddr, demultiplexer_3_out1, Finished);
  D_Flip_Flop IDLE (.clk(Clock), .D(or_1_out), .Q(IDLE_q), .preset(CLR));  // open: Qn, en, reset
  Demultiplexer #(.enable("false")) demultiplexer_1 (.out0(Load), .out1(Finished), .in(IDLE_q), .sel(End));
  D_Flip_Flop While (.clk(Clock), .D(or_2_out), .Q(While_q), .reset(CLR));  // open: Qn, preset, en
  or or_2 (or_2_out, Write, Load);
  RAM_part #(.addrWidth(18), .dataWidth(32)) ram_1 (
    .addr({Address, CurrentAddress_q[1:0]}), .data(Data), .clk(Clock));  // open: sel, ld, clr
  Demultiplexer #(.enable("false")) demultiplexer_2 (
    .out0(Write), .out1(demultiplexer_2_out1), .in(While_q), .sel(WriteEnd));
  Decoder #(.select(2)) decoder_1 (
    .out0(Mask[0]), .out1(Mask[1]), .out2(Mask[2]), .out3(Mask[3]), .sel(CurrentAddress_q[1:0]));  // open: en
  Demultiplexer #(.enable("false")) demultiplexer_3 (
    .out0(IncAddr), .out1(demultiplexer_3_out1), .in(demultiplexer_2_out1), .sel(End));
  Counter #(.width(4), .max('hf)) counter_1 (
    .load(Load), .D(WriteTime), .count(Write), .Q(counter_1_q), .clk(Clock));  // open: carry, clr
  Comparator #(.width(32)) comparator_1 (.a(Data), .b({32{1'b1}}), .eq(End));  // open: gt, lt
  Comparator #(.width(4)) comparator_2 (.a(4'b0000), .b(counter_1_q), .eq(WriteEnd));  // open: gt, lt

  // Other names for the same wires on the sheet: CLK = Clock; Count = Write; WT[3:0] = WriteTime
endmodule

module Register_File (
  input  [4:0] INPUT,
  input  [31:0] in_2,
  input  [4:0] in_3,
  input  [31:0] in_4,
  input  [31:0] in_5,
  input  in_6,
  input  in_7,
  input  [4:0] in_8,
  input  in_9,
  input  in_10,
  output [31:0] out_11,
  output [31:0] out_12,
  output [31:0] out_13,
  output [31:0] out_14
);

  wire e1, e2, e3, e4, e5, e6, e7, e8, e9, e10, e11, e12, e13, e14, e15, e16, e17, e18, e19, e20, e21, e22,
       e23, e24, e25, e26, e27, e28, e29, e30, e31;
  wire [31:0] s1, s2, s3, s4, s5, s6, s7, s8, s9, s10, s11, s12, s13, s14, s15, s16, s17, s18, s19, s20, s21,
       s22, s23, s24, s25, s26, s27, s28, s29, s30, s31;

  Register #(.width(32)) R1 (.D(in_2), .en(e1), .Q(s1), .clk(in_6), .clr(in_7));
  Register #(.width(32)) R7 (.D(in_2), .en(e7), .Q(s7), .clk(in_6), .clr(in_7));
  Register #(.width(32)) R13 (.D(in_2), .en(e13), .Q(s13), .clk(in_6), .clr(in_7));
  Register #(.width(32)) R19 (.D(in_2), .en(e19), .Q(s19), .clk(in_6), .clr(in_7));
  Register #(.width(32)) R25 (.D(in_2), .en(e25), .Q(s25), .clk(in_6), .clr(in_7));
  Register #(.width(32)) R31 (.D(in_2), .en(e31), .Q(s31), .clk(in_6), .clr(in_7));
  Register #(.width(32)) R2 (.D(in_2), .en(e2), .Q(s2), .clk(in_6), .clr(in_7));
  Register #(.width(32)) R8 (.D(in_2), .en(e8), .Q(s8), .clk(in_6), .clr(in_7));
  Register #(.width(32)) R14 (.D(in_2), .en(e14), .Q(s14), .clk(in_6), .clr(in_7));
  Register #(.width(32)) R20 (.D(in_2), .en(e20), .Q(s20), .clk(in_6), .clr(in_7));
  Register #(.width(32)) R26 (.D(in_2), .en(e26), .Q(s26), .clk(in_6), .clr(in_7));
  Register #(.width(32)) Hi (.D(in_4), .en(in_10), .Q(out_11), .clk(in_6), .clr(in_7));
  Register #(.width(32)) R3 (.D(in_2), .en(e3), .Q(s3), .clk(in_6), .clr(in_7));
  Register #(.width(32)) R9 (.D(in_2), .en(e9), .Q(s9), .clk(in_6), .clr(in_7));
  Register #(.width(32)) R15 (.D(in_2), .en(e15), .Q(s15), .clk(in_6), .clr(in_7));
  Register #(.width(32)) R21 (.D(in_2), .en(e21), .Q(s21), .clk(in_6), .clr(in_7));
  Register #(.width(32)) R27 (.D(in_2), .en(e27), .Q(s27), .clk(in_6), .clr(in_7));
  Register #(.width(32)) R4 (.D(in_2), .en(e4), .Q(s4), .clk(in_6), .clr(in_7));
  Register #(.width(32)) R10 (.D(in_2), .en(e10), .Q(s10), .clk(in_6), .clr(in_7));
  Register #(.width(32)) R16 (.D(in_2), .en(e16), .Q(s16), .clk(in_6), .clr(in_7));
  Register #(.width(32)) R22 (.D(in_2), .en(e22), .Q(s22), .clk(in_6), .clr(in_7));
  Register #(.width(32)) R28 (.D(in_2), .en(e28), .Q(s28), .clk(in_6), .clr(in_7));
  Register #(.width(32)) Lo (.D(in_5), .en(in_10), .Q(out_12), .clk(in_6), .clr(in_7));
  Register #(.width(32)) R5 (.D(in_2), .en(e5), .Q(s5), .clk(in_6), .clr(in_7));
  Register #(.width(32)) R11 (.D(in_2), .en(e11), .Q(s11), .clk(in_6), .clr(in_7));
  Register #(.width(32)) R17 (.D(in_2), .en(e17), .Q(s17), .clk(in_6), .clr(in_7));
  Register #(.width(32)) R23 (.D(in_2), .en(e23), .Q(s23), .clk(in_6), .clr(in_7));
  Register #(.width(32)) R29 (.D(in_2), .en(e29), .Q(s29), .clk(in_6), .clr(in_7));
  Register #(.width(32)) R6 (.D(in_2), .en(e6), .Q(s6), .clk(in_6), .clr(in_7));
  Register #(.width(32)) R12 (.D(in_2), .en(e12), .Q(s12), .clk(in_6), .clr(in_7));
  Register #(.width(32)) R18 (.D(in_2), .en(e18), .Q(s18), .clk(in_6), .clr(in_7));
  Register #(.width(32)) R24 (.D(in_2), .en(e24), .Q(s24), .clk(in_6), .clr(in_7));
  Register #(.width(32)) R30 (.D(in_2), .en(e30), .Q(s30), .clk(in_6), .clr(in_7));
  Multiplexer #(.select(5), .width(32), .enable("false")) multiplexer_1 (
    .in0({32{1'b0}}), .in1(s1), .in2(s2), .in3(s3), .in4(s4), .in5(s5), .in6(s6), .in7(s7), .in8(s8),
    .in9(s9), .in10(s10), .in11(s11), .in12(s12), .in13(s13), .in14(s14), .in15(s15), .in16(s16), .in17(s17),
    .in18(s18), .in19(s19), .in20(s20), .in21(s21), .in22(s22), .in23(s23), .in24(s24), .in25(s25),
    .in26(s26), .in27(s27), .in28(s28), .in29(s29), .in30(s30), .in31(s31), .out(out_13), .sel(INPUT));
  Multiplexer #(.select(5), .width(32), .enable("false")) multiplexer_2 (
    .in0({32{1'b0}}), .in1(s1), .in2(s2), .in3(s3), .in4(s4), .in5(s5), .in6(s6), .in7(s7), .in8(s8),
    .in9(s9), .in10(s10), .in11(s11), .in12(s12), .in13(s13), .in14(s14), .in15(s15), .in16(s16), .in17(s17),
    .in18(s18), .in19(s19), .in20(s20), .in21(s21), .in22(s22), .in23(s23), .in24(s24), .in25(s25),
    .in26(s26), .in27(s27), .in28(s28), .in29(s29), .in30(s30), .in31(s31), .out(out_14), .sel(in_3));
  Demultiplexer #(.select(5), .enable("false")) demultiplexer_1 (
    .out1(e1), .out2(e2), .out3(e3), .out4(e4), .out5(e5), .out6(e6), .out7(e7), .out8(e8), .out9(e9),
    .out10(e10), .out11(e11), .out12(e12), .out13(e13), .out14(e14), .out15(e15), .out16(e16), .out17(e17),
    .out18(e18), .out19(e19), .out20(e20), .out21(e21), .out22(e22), .out23(e23), .out24(e24), .out25(e25),
    .out26(e26), .out27(e27), .out28(e28), .out29(e29), .out30(e30), .out31(e31), .in(in_9), .sel(in_8));  // open: out0

  // Other names for the same wires on the sheet: A[31:0] = out_13; B[31:0] = out_14; Clock = in_6; DW[4:0] = in_8;
  //   H[31:0] = in_4; Hi[31:0] = out_11; Inp[31:0] = in_2; L[31:0] = in_5; L___H_R_W = in_10; Lo[31:0] = out_12;
  //   R_W = in_9; Reset = in_7; S_A[4:0] = INPUT; S_B[4:0] = in_3

  // Notes on the sheet:
  //   Hi
  //   REGISTER
  //   Special Registers
  //   Lo
  //   R
  //   F
  //   EGISTER
  //   ILE
  //   OUTPUT SELECTION
  //   WRITE SELECTION
  //   OUTPUT
endmodule

module ALU (
  input  [31:0] in_1,
  input  [31:0] in_2,
  input  [3:0] in_3,
  output [31:0] out_4,
  output [31:0] out_5,
  output out_6,
  output out_7
);

  wire comparator_1_lt, comparator_2_lt, En;
  wire [31:0] AND, COMP, COMP_U, D_C, D_CU, DIV, DIV_U, M_C, M_CU, MUL, MUL_U, NOR, OR, SUB, SUM, XOR;

  Adder #(.width(32)) adder_1 (.a(in_1), .b(in_2), .out(SUM));  // open: cin, cout
  Divider_S divider_s_1 (.in_1(in_1), .in_2(in_2), .out_3(DIV), .out_4(D_C));
  Comparator #(.width(32)) comparator_1 (.a(in_1), .b(in_2), .lt(comparator_1_lt));  // open: gt, eq
  assign COMP = {{31{1'b0}}, comparator_1_lt};  // Bit_Extender bit_extender_1
  Multiplexer #(.select(2), .width(32)) multiplexer_1 (
    .in0(M_C), .in1(M_CU), .in2(D_C), .in3(D_CU), .out(out_5), .sel(in_3[1:0]), .en(En));
  nor nor_1 (En, in_3[2], in_3[3]);
  Subtractor #(.width(32)) subtractor_1 (.a(in_1), .b(in_2), .out(SUB));  // open: bin, bout
  Comparator #(.width(32), .mode("unsigned")) comparator_2 (.a(in_1), .b(in_2), .lt(comparator_2_lt));  // open: gt, eq
  Multiplier_S multiplier_s_1 (.in_1(in_1), .in_2(in_2), .out_3(MUL), .out_4(M_C));
  assign COMP_U = {{31{1'b0}}, comparator_2_lt};  // Bit_Extender bit_extender_2
  Multiplexer #(.select(4), .width(32), .enable("false")) multiplexer_2 (
    .in0(MUL), .in1(MUL_U), .in2(DIV), .in3(DIV_U), .in4(AND), .in5(SUB), .in6(XOR), .in7(SUM), .in8(OR),
    .in9(COMP_U), .in10(NOR), .in11(COMP), .in12(in_2), .in13(in_1), .out(out_4), .sel(in_3));  // open: in14, in15
  Comparator #(.width(32)) comparator_3 (.a(out_4), .b({32{1'b0}}), .eq(out_6), .lt(out_7));  // open: gt
  assign AND = in_1 & in_2;  // AND_Gate and_1, 32 bits wide
  Multiplier #(.width(32)) multiplier_1 (.a(in_1), .b(in_2), .out(MUL_U), .cout(M_CU));  // open: cin
  assign XOR = in_1 ^ in_2;  // XOR_Gate xor_1, 32 bits wide
  assign OR = in_1 | in_2;  // OR_Gate or_1, 32 bits wide
  Divider #(.width(32)) divider_1 (.a(in_1), .b(in_2), .out(DIV_U), .rem(D_CU));  // open: upper
  assign NOR = ~(in_1 | in_2);  // NOR_Gate nor_2, 32 bits wide

  // Other names for the same wires on the sheet: A[31:0] = in_1; B[31:0] = in_2; Carry[31:0] = out_5; N_flag = out_7;
  //   OP[3:0] = in_3; S_C[1:0] = in_3[1:0]; S[31:0] = out_4; ZERO_flag = out_6

  // Notes on the sheet:
  //   INPUT
  //   OPERACIONES
  //   SUMA
  //   DIVISIÓN
  //   COMPARADOR
  //   Aritmetic
  //   Carry
  //   -
  //   RESTA
  //   MULTIPLICACIÓN
  //   COMPARADOR U
  //   Logic
  //   Unit
  //   AND LOGIC
  //   MULTIPLICACIÓN U
  //   XOR
  //   (ALU)
  //   OR LOGIC
  //   DIVISIÓN U
  //   NOR
  //   OUTPUT
endmodule

module Instruction_Decoder (
  input  [31:0] in_1,
  output [25:0] out_2,
  output [4:0] out_3,
  output [4:0] out_4,
  output [4:0] out_5,
  output [15:0] out_6,
  output [5:0] out_7,
  output [5:0] out_8
);


  assign out_2 = in_1[25:0];
  assign out_3 = in_1[25:21];
  assign out_4 = in_1[20:16];
  assign out_5 = in_1[15:11];
  assign out_6 = in_1[15:0];
  assign out_7 = in_1[5:0];
  assign out_8 = in_1[31:26];

  // Other names for the same wires on the sheet: Const[15:0] = in_1[15:0]; Destino_Salto[25:0] = in_1[25:0];
  //   Func_Code[5:0] = in_1[5:0]; Inst[31:0] = in_1; X[4:0] = in_1[10:6]; Rd[4:0] = in_1[15:11];
  //   Rt[4:0] = in_1[20:16]; Rs[4:0] = in_1[25:21]; Op_Code[5:0] = in_1[31:26]

  // Notes on the sheet:
  //   INPUT
  //   Instruction Decoder
  //   OUTPUT
endmodule

module Branch_Control (
  input  [25:0] in_1,
  input  [31:0] in_2,
  input  [31:0] in_3,
  input  [31:0] in_4,
  input  in_5,
  input  in_6,
  input  in_7,
  input  [2:0] in_8,
  output [31:0] out_9
);

  wire [1:0] Sel;
  wire [31:0] I_Type, Next, shifter_1_out;

  Adder #(.width(32)) adder_1 (.a(in_2), .b(32'h4), .out(Next));  // open: cin, cout
  Jump_Sel jump_sel_1 (.jump(in_5), .B2(in_8[2]), .B1(in_8[1]), .B0(in_8[0]), .Z(in_7), .N(in_6), .out_7(Sel));
  Shifter #(.width(32)) shifter_1 (.in(in_3), .\dist (5'b00010), .out(shifter_1_out));
  Multiplexer #(.select(2), .width(32), .enable("false")) multiplexer_1 (
    .in0(Next), .in1(I_Type), .in2(in_4), .in3({in_2[31:28], in_1, 2'b00}), .out(out_9), .sel(Sel));
  Adder #(.width(32)) adder_2 (.a(shifter_1_out), .b(Next), .out(I_Type));  // open: cin, cout

  // Other names for the same wires on the sheet: B0 = in_8[0]; Branch_Code[2:0] = in_8; B1 = in_8[1]; B2 = in_8[2];
  //   D_S[31:2] = {in_2[31:28], in_1}; Destino_Salto[25:0] = in_1; Complement[3:0] = in_2[31:28]; PC[31:0] = in_2;
  //   Jr[31:0] = in_4; Jump = in_5; N = in_6; Off[31:0] = in_3; PC_new[31:0] = out_9; Z = in_7

  // Notes on the sheet:
  //   Input
  //   Next 
  //   Branch Control
  //   Output
  //   I-Type
  //   J-Type
endmodule

module Data_Path (
  input  Input,
  input  in_2,
  input  [31:0] in_3,
  input  [31:0] in_4,
  input  [31:0] in_5,
  input  [31:0] in_6,
  input  [6:0] in_7,
  input  [2:0] in_8,
  input  [3:0] in_9,
  input  [2:0] in_10,
  input  [2:0] in_11,
  input  [1:0] in_12,
  input  in_13,
  input  in_14,
  input  in_15,
  input  in_16,
  input  in_17,
  input  in_18,
  input  in_19,
  input  in_20,
  input  in_21,
  input  in_22,
  input  in_23,
  output [31:0] out_24,
  output [15:0] out_25,
  output [3:0] out_26,
  output [6:0] out_27,
  output [5:0] out_28,
  output [5:0] out_29
);

  wire N, Z;
  wire [4:0] DW, Rd, Rs, Rt, S_A, S_B;
  wire [15:0] Cte;
  wire [25:0] D_S;
  wire [31:0] A, ALU_Hi, ALU_Out, B, B_ALU, B_RF, Cte_Ext, Data_Out, Hi, Hi_ALU, Hi_RF, Inp, Inst,
       Instruction, KBD, kbd_t, Lo, Lo_RF, multiplexer_7_out, Out_ALU, PC, PC_star, Rnd;
  wire [31:7] A_RF;

  Multiplexer #(.select(3), .width(32), .enable("false")) multiplexer_1 (
    .in0(B), .in1(Cte_Ext), .in2(Hi), .in3(Lo), .in4(32'h4), .in5({32{1'b0}}), .out(B_ALU), .sel(in_11));  // open: in6, in7
  ALU alu_1 (.in_1(A), .in_3(in_9), .in_2(B_ALU), .out_4(ALU_Out), .out_5(Hi_ALU), .out_6(Z), .out_7(N));
  Register #(.width(32)) u_ALU_Out (.D(ALU_Out), .en(in_20), .Q(Out_ALU), .clk(Input));  // open: clr
  Register #(.width(32)) u_Hi_ALU (.D(Hi_ALU), .en(in_20), .Q(ALU_Hi), .clk(Input));  // open: clr
  assign Cte_Ext = {{16{Cte[15]}}, Cte};  // Bit_Extender bit_extender_1
  Random #(.width(32)) random_1 (.clk(Input), .out(Rnd));  // open: next, clr
  Multiplexer #(.width(32), .enable("false")) multiplexer_2 (.in0({32{1'b1}}), .in1(KBD), .out(kbd_t), .sel(in_22));
  Multiplexer #(.select(2), .width(5), .enable("false")) multiplexer_3 (
    .in0(Rt), .in1(Rd), .in2({5{1'b1}}), .out(DW), .sel(in_12));  // open: in3
  Multiplexer #(.width(5), .enable("false")) multiplexer_4 (.in0(Rs), .in1({5{1'b1}}), .out(S_A), .sel(in_13));
  Multiplexer #(.width(5), .enable("false")) multiplexer_5 (.in0(Rt), .in1(Rs), .out(S_B), .sel(in_14));
  Register_File register_file_1 (
    .INPUT(S_A), .in_2(Inp), .in_3(S_B), .in_4(ALU_Hi), .in_5(Out_ALU), .in_6(Input), .in_7(in_2), .in_8(DW),
    .in_9(in_15), .in_10(in_16), .out_12(Lo_RF), .out_13({A_RF, out_27}), .out_14(B_RF), .out_11(Hi_RF));
  Multiplexer #(.select(3), .width(32), .enable("false")) multiplexer_6 (
    .in0(Out_ALU), .in1(Data_Out), .in2(Lo), .in3(Hi), .in4(Rnd), .in5(kbd_t), .out(Inp), .sel(in_8));  // open: in6, in7
  Register #(.width(32)) u_A (.D({A_RF, out_27}), .en(in_21), .Q(A), .clk(Input));  // open: clr
  Register #(.width(32)) u_B (.D(B_RF), .en(in_21), .Q(B), .clk(Input));  // open: clr
  assign KBD = {{25{1'b0}}, in_7};  // Bit_Extender bit_extender_2
  Register #(.width(32)) u_Hi (.D(Hi_RF), .en(in_21), .Q(Hi), .clk(Input));  // open: clr
  Register #(.width(32)) u_Lo (.D(Lo_RF), .en(in_21), .Q(Lo), .clk(Input));  // open: clr
  Multiplexer #(.width(32), .enable("false")) multiplexer_7 (
    .in0(PC), .in1(Out_ALU), .out(multiplexer_7_out), .sel(in_23));
  Branch_Control branch_control_1 (
    .in_1(D_S), .in_2(PC), .in_3(Cte_Ext), .in_4(A), .in_5(in_17), .in_6(N), .in_7(Z), .in_8(in_10),
    .out_9(PC_star));
  Instruction_Data_Memory instruction_data_memory_1 (
    .in_1(in_3), .in_2(in_5), .in_3(in_4), .in_4(in_6), .in_6(multiplexer_7_out), .in_5(B), .out_7(Inst),
    .out_8(out_24), .out_9(out_25), .out_10(out_26));
  Instruction_Decoder instruction_decoder_1 (
    .in_1(Instruction), .out_2(D_S), .out_3(Rs), .out_4(Rt), .out_5(Rd), .out_6(Cte), .out_7(out_29),
    .out_8(out_28));
  Register #(.width(32)) Ins (.D(Inst), .en(in_19), .Q(Instruction), .clk(Input));  // open: clr
  Register #(.width(32)) Data (.D(Inst), .en(in_18), .Q(Data_Out), .clk(Input));  // open: clr
  Register #(.width(32)) u_PC (.D(PC_star), .en(in_17), .Q(PC), .clk(Input), .clr(in_2));

  // Other names for the same wires on the sheet: A_RF[6:0] = out_27; TTY[6:0] = out_27; ALU_OP[3:0] = in_9;
  //   B_C[2:0] = in_10; Clock = Input; DATA_RAM[31:0] = out_24; Data_W = in_18; DIR_RAM[15:0] = out_25;
  //   Func_Code[5:0] = out_29; H_L_W = in_16; I0[31:0] = in_3; I1[31:0] = in_4; I2[31:0] = in_5; I3[31:0] = in_6;
  //   I_v_D = in_23; Ins_W = in_19; Kbd_Available = in_22; KBD_DATA[6:0] = in_7; L_A_B = in_21; L_Hi = in_20;
  //   MASK[3:0] = out_26; Op_Code[5:0] = out_28; PC_enable = in_17; R_W__RF = in_15; Reset = in_2; S_A_RF = in_13;
  //   S_B_ALU[2:0] = in_11; S_B_RF = in_14; S_DATA__RF[2:0] = in_8; S_DW_RF[1:0] = in_12

  // Notes on the sheet:
  //   ALU
  //   Register File
  //   Data Path
  //   Instruction Memory
  //   Branch Control
  //   Instruction Decoder
  //   Program Counter
  //   Output
endmodule

module Instruction_Data_Memory (
  input  [31:0] in_1,
  input  [31:0] in_2,
  input  [31:0] in_3,
  input  [31:0] in_4,
  input  [31:0] in_5,
  input  [31:0] in_6,
  output [31:0] out_7,
  output [31:0] out_8,
  output [15:0] out_9,
  output [3:0] out_10
);

  wire not_1_out, not_2_out, not_3_out, not_4_out;

  and and_1 (out_10[3], in_6[2], in_6[3]);
  not not_1 (not_1_out, in_6[2]);
  and and_2 (out_10[2], not_1_out, in_6[3]);
  not not_2 (not_2_out, in_6[3]);
  and and_3 (out_10[1], not_2_out, in_6[2]);
  not not_3 (not_3_out, in_6[2]);
  and and_4 (out_10[0], not_3_out, not_4_out);
  not not_4 (not_4_out, in_6[3]);
  Multiplexer #(.select(2), .width(32), .enable("false")) multiplexer_1 (
    .in0(in_1), .in1(in_3), .in2(in_2), .in3(in_4),
    .out({out_7[7:0], out_7[15:8], out_7[23:16], out_7[31:24]}), .sel(in_6[3:2]));

  assign out_8 = {in_5[7:0], in_5[15:8], in_5[23:16], in_5[31:24]};
  assign out_9 = in_6[19:4];

  // Other names for the same wires on the sheet: Address[31:0] = in_6; Bank_SEL[1:0] = in_6[3:2];
  //   Address_to_RAM[15:0] = in_6[19:4]; I0[31:0] = in_1; I1[31:0] = in_3; I2[31:0] = in_2; I3[31:0] = in_4;
  //   MASK[3:0] = out_10; RD[31:0] = out_7; Data[31:0] = in_5;
  //   WD[31:0] = {in_5[7:0], in_5[15:8], in_5[23:16], in_5[31:24]}

  // Notes on the sheet:
  //   Input 
  //   Instruction D-M 
  //   Little-Endian
  //   Output
endmodule

module Jump_Sel (
  input  jump,
  input  B2,
  input  B1,
  input  B0,
  input  Z,
  input  N,
  output [1:0] out_7
);

  wire and_2_out, and_3_out, and_4_out, and_5_out, and_6_out, and_7_out, not_1_out, not_2_out, not_3_out,
       not_4_out, not_5_out, not_6_out, not_7_out, not_8_out, not_9_out, not_10_out, not_11_out;

  and and_1 (out_7[1], jump, B2, B1);
  not not_1 (not_1_out, B2);
  not not_2 (not_2_out, B0);
  not not_3 (not_3_out, Z);
  not not_4 (not_4_out, B2);
  not not_5 (not_5_out, Z);
  not not_6 (not_6_out, B0);
  not not_7 (not_7_out, Z);
  not not_8 (not_8_out, N);
  not not_9 (not_9_out, B1);
  not not_10 (not_10_out, Z);
  not not_11 (not_11_out, B0);
  and and_2 (and_2_out, jump, not_1_out, B0, Z);
  and and_3 (and_3_out, jump, B1, not_2_out, not_3_out);
  and and_4 (and_4_out, jump, not_4_out, B1, not_5_out, N);
  and and_5 (and_5_out, jump, B2, not_6_out, not_7_out, not_8_out);
  and and_6 (and_6_out, jump, B2, not_9_out, B0, not_10_out, N);
  and and_7 (and_7_out, jump, B2, B1, not_11_out);
  or or_1 (out_7[0], and_2_out, and_3_out, and_4_out, and_5_out, and_6_out, and_7_out);
endmodule
